# Fritzing sketch Circuit_v1 (1) (saved by Fritzing 0.9.4)

parts:
  Raspberry_Pi_1 = Raspberry Pi 3 [part_number=RPI-3-V1.2]
  RPi_Camera_(CSI) = Rasberry Pi NIOR Camera [chip_label=IC package="DIP (Dual Inline) [THT]"]  # not connected
  U1 = LM2596 step down module
  S1 = Round Pushbutton
  GLCD_128x1 = 128 x 64 Graphic LCD  # not connected
  WeMos_D1_Mini_WS2812B_RGB_Shield1 = WeMos D1 Mini WS2812B RGB Shield
  VCC1 = Battery
  3-pins_Hall_Effect_Sensor1 = mystery part, 3 pins [chip_label="Hall Effect Sensor"]
  3-pins_Hall_Effect_Sensor4 = mystery part, 3 pins [chip_label="Hall Effect Sensor"]
  S2 = Limit Switch [package="Breakout Board"]
  J1 = Basic Servo
  J2 = Basic Servo

nets:
  N1: Raspberry_Pi_1.GND, U1.IN-, U1.OUT-, VCC1.-
  N2: Raspberry_Pi_1.5V, U1.OUT+
  N3: U1.IN+, S1.leg1
  N4: S1.leg0, VCC1.+
  VCC: WeMos_D1_Mini_WS2812B_RGB_Shield1.5V, 3-pins_Hall_Effect_Sensor1.pin2, 3-pins_Hall_Effect_Sensor4.pin2, S2.V, J1.vcc, J2.vcc
  N5: WeMos_D1_Mini_WS2812B_RGB_Shield1.D1, J2.pulse
  N6: WeMos_D1_Mini_WS2812B_RGB_Shield1.D2, J1.pulse
  N7: WeMos_D1_Mini_WS2812B_RGB_Shield1.D6, S2.S
  N8: WeMos_D1_Mini_WS2812B_RGB_Shield1.D7, 3-pins_Hall_Effect_Sensor4.pin3
  N9: WeMos_D1_Mini_WS2812B_RGB_Shield1.D8, 3-pins_Hall_Effect_Sensor1.pin3
  GND: WeMos_D1_Mini_WS2812B_RGB_Shield1.G, 3-pins_Hall_Effect_Sensor1.pin1, 3-pins_Hall_Effect_Sensor4.pin1, S2.G, J1.gnd, J2.gnd

notes:
  Arduino Nano
  Подключена по USB к Raspberry Pi (Vin, GND)
  OV5647
  Камера для Raspberry Pi
  Подключена по шине CSI
  3.5 дюймовый дисплей RPi. Соединятеся с Raspberry Pi 4b через пины.
  Raspberry Pi High Quality.
  Соединяется с Raspberry Pi по шине CIS
  Raspberry Pi 4b
  Реализует управление устройством и алгоритмы системы технического зрения
  ESP 8266 Wemos D1 mini
  Реализует вращение барабаном, подъем площадки, управление датчиком Холла
  Запитка по USB от Raspberry Pi 4b
  сервопривод SG90
  Используется для переворота площадки
  сервопривод постоянного вращения Feetech FTR90
  используется для вращения барабана
  Понижающий преоразователь DC DC LM2596
  Понижает и стабилизирует питание 7.4В -> 5В
  Кнопка питания
  Аккумулятор Li-ion 18650 2s 2p
  Питание устройства
  Датчики Холла A3144E
  Используются для отслеживания положения барабана
  Концевик RAMPS 1.4
  Используется для отслеживания момента полного опускания подъемной площадки

custom parts:
  Rasberry Pi NIOR Camera: Camera
  LM2596 step down module: LM2596 DC-DC step down power supply module 3 A.
  Limit Switch: Generic limit switch commonly found on 3D printers. Typical lever microswitch mounted on a PCB board with a 3 pin JST XH connector.
